# Fritzing sketch arduino-puzzle-box (saved by Fritzing 0.9.2b)
breadboards: 1

parts:
  Part1 = Arduino Uno (Rev3)
  LED1 = LED - 5mm [color="Green (570nm)" package="5 mm [THT]"]
  LED2 = LED - 5mm [color="Green (570nm)" package="5 mm [THT]"]
  LED3 = LED - 5mm [color="Green (570nm)" package="5 mm [THT]"]
  LED4 = LED - 5mm [color="Green (570nm)" package="5 mm [THT]"]
  LED5 = LED - 5mm [color="Red (660nm)" package="5 mm [THT]"]
  S1 = Pushbutton [package="[THT]"]
  R1 = Photocell (LDR) [package=THT]
  R2 = Resistor [tolerance=±5% resistance=1k package=THT]
  R3 = Resistor [tolerance=±5% resistance=1k package=THT]
  R4 = Resistor [tolerance=±5% resistance=1k package=THT]
  R5 = Resistor [tolerance=±5% resistance=1k package=THT]
  R6 = Resistor [tolerance=±5% resistance=10k package=THT]
  R7 = Resistor [tolerance=±5% resistance=1k package=THT]
  R8 = Resistor [tolerance=±5% resistance=10k package=THT]
  S2 = Tilt Switch [package=THT]
  R10 = Resistor [tolerance=±5% resistance=1k package=THT]
  J1 = Basic Servo
  J2 = Piezo Speaker
  R9 = Rotary Potentiometer (Large) [maximum_resistance=100kΩ package=THT]

nets:
  N1: Part1.A0, R1.pin_0, R7.Pin_0
  N2: Part1.A1, R9.wiper
  N3: Part1.A2, S2.Pin_2
  N4: Part1.D8, J1.pulse
  N5: Part1.D9_PWM, J2.pin2
  N6: Part1.D2, R6.Pin_0
  N7: Part1.D3_PWM, R5.Pin_0
  N8: Part1.D4, R4.Pin_0
  N9: Part1.D5_PWM, R3.Pin_0
  N10: Part1.D6_PWM, R2.Pin_0
  N11: Part1.D7, S1.Pin_1, S1.Pin_2, R8.Pin_1
  5V: Part1.5V, S1.Pin_3, S1.Pin_4, R1.pin_1, R10.Pin_1, J1.vcc, R9.leg2
  GND: Part1.GND, LED2.cathode, LED3.cathode, LED4.cathode, LED5.cathode, R7.Pin_1, R8.Pin_0, J1.gnd, R9.leg1
  N12: LED1.anode, R6.Pin_1
  N13: LED2.anode, R5.Pin_1
  N14: LED3.anode, R4.Pin_1
  N15: LED4.anode, R3.Pin_1
  N16: LED5.anode, R2.Pin_1
  N17: S2.Pin_1, R10.Pin_0
